// Logisim project cpu.circ as structural Verilog: 3 circuits, main circuit datapath
module ALU (
  input  [7:0] A,
  input  [7:0] B,
  input  [2:0] S,
  output [7:0] R,
  output ZF,
  output VF
);

  wire A7, and_6_out, and_7_out, APlusB, ASubB, B7, IncA, IncB, not_5_out, not_6_out, not_7_out, Not_S0,
       Not_S1, Not_S2, or_2_out, or_3_out, R7;
  wire [6:0] adder_1_out, multiplexer_1_out, multiplexer_2_out;
  wire [7:0] and_3_out, multiplexer_3_out, not_1_out, or_1_out;

  assign not_1_out = ~B;  // NOT_Gate not_1, 8 bits wide
  and and_1 (IncA, Not_S2, S[1], Not_S0);
  and and_2 (IncB, Not_S2, S[1], S[0]);
  Multiplexer #(.width(8)) multiplexer_1 (.in0(A), .in1(8'h1), .out({A7, multiplexer_1_out}), .sel(IncB));
  Multiplexer #(.width(8)) multiplexer_2 (
    .in0(multiplexer_3_out), .in1(not_1_out), .out({B7, multiplexer_2_out}), .sel(ASubB));
  Multiplexer #(.width(8)) multiplexer_3 (.in0(B), .in1(8'h1), .out(multiplexer_3_out), .sel(IncA));
  assign and_3_out = A & B;  // AND_Gate and_3, 8 bits wide
  assign or_1_out = A | B;  // OR_Gate or_1, 8 bits wide
  Adder adder_1 (
    .a({A7, multiplexer_1_out}), .b({B7, multiplexer_2_out}), .out({R7, adder_1_out}), .cin(ASubB));  // open: cout
  not not_2 (Not_S0, S[0]);
  not not_3 (Not_S1, S[1]);
  not not_4 (Not_S2, S[2]);
  and and_4 (APlusB, S[2], Not_S1, Not_S0);
  and and_5 (ASubB, S[2], Not_S1, S[0]);
  Multiplexer #(.select(3), .width(8)) multiplexer_4 (
    .in0(A), .in1(B), .in2({R7, adder_1_out}), .in3({R7, adder_1_out}), .in4({R7, adder_1_out}),
    .in5({R7, adder_1_out}), .in6(and_3_out), .in7(or_1_out), .out(R), .sel(S));
  not not_5 (not_5_out, A7);
  not not_6 (not_6_out, B7);
  not not_7 (not_7_out, R7);
  and and_6 (and_6_out, not_5_out, R7, not_6_out);
  and and_7 (and_7_out, A7, not_7_out, B7);
  nor nor_1 (ZF, R[0], R[1], R[2], R[3], R[4], R[5], R[6], R[7]);
  or or_2 (or_2_out, and_6_out, and_7_out);
  or or_3 (or_3_out, IncA, IncB, APlusB, ASubB);
  and and_8 (VF, or_2_out, or_3_out);

  // Notes on the sheet:
  //   Opcode Detectors - used to detect which arithmetic op we are performing
  //   Extract MSB of operands
  //   and result for overflow
  //   detection.
  //   8-bit ALU with zero and overflow detection
  //   Author: RR
  //   Logic for VF: We performed addition,
  //   increment, or subtraction and there was a sign
  //   mismatch between operands and result
endmodule

module datapath (
  input  [7:0] INP,
  input  RST,
  output HALT,
  output [7:0] DISPBits
);

  wire AEnable, BEnable, CLK, DISPEnable, MBREnable, PCEnable;
  wire [1:0] BSelect;
  wire [2:0] ALUSelect;
  wire [4:0] MBRR;
  wire [7:0] A_q, alu_1_r, B_q, Data, multiplexer_1_out, PC_q;
  wire [7:5] MBR_q;

  Register A (.D(alu_1_r), .en(AEnable), .clk(CLK), .Q(A_q), .clr(RST));
  Register B (.D(alu_1_r), .en(BEnable), .clk(CLK), .Q(B_q), .clr(RST));
  Register MBR (.D(Data), .en(MBREnable), .clk(CLK), .Q({MBR_q, MBRR}), .clr(RST));
  Register PC (.D(alu_1_r), .en(PCEnable), .clk(CLK), .Q(PC_q), .clr(RST));
  Register DISP (.D(alu_1_r), .en(DISPEnable), .clk(CLK), .Q(DISPBits), .clr(RST));
  Hex_Digit_Display hex_digit_display_1 (.value(DISPBits[7:4]));  // open: dp
  RAM #(.asyncread("true"), .databus("bidir")) ProgramStore (.addr(PC_q), .data(Data));  // open: we, oe, clk
  Hex_Digit_Display hex_digit_display_2 (.value(DISPBits[3:0]));  // open: dp
  Clock clock_1 (.out(CLK));
  Multiplexer #(.select(2), .width(8)) multiplexer_1 (
    .in0(B_q), .in1({MBR_q, MBRR}), .in2(PC_q), .in3(INP), .out(multiplexer_1_out), .sel(BSelect));
  ALU alu_1 (.A(A_q), .B(multiplexer_1_out), .S(ALUSelect), .R(alu_1_r));  // open: ZF, VF
  control control_1 (
    .FROM_MBR(MBRR), .CLK(CLK), .RST(RST), .WRITES({AEnable, BEnable, MBREnable, PCEnable, DISPEnable}),
    .BSelect(BSelect), .ALUSelect(ALUSelect), .HALT(HALT));
endmodule

module control (
  input  [4:0] FROM_MBR,
  input  CLK,
  input  RST,
  output [4:0] WRITES,
  output [1:0] BSelect,
  output [2:0] ALUSelect,
  output HALT
);

  wire DSP, not_1_out;
  wire [4:0] multiplexer_1_out, register_1_q;
  wire [15:0] rom_1_data;
  wire [15:11] register_2_q;

  Multiplexer #(.width(5)) multiplexer_1 (.in0(register_2_q), .in1(FROM_MBR), .out(multiplexer_1_out), .sel(DSP));
  Register #(.width(5)) register_1 (.D(multiplexer_1_out), .en(1'b1), .clk(CLK), .Q(register_1_q), .clr(RST));
  ROM #(.addrWidth(5), .dataWidth(16)) rom_1 (.addr(register_1_q), .data(rom_1_data));
  Register #(.trigger("falling"), .width(16)) register_2 (
    .D(rom_1_data), .en(1'b1), .clk(CLK), .Q({register_2_q, DSP, ALUSelect, BSelect, WRITES}), .clr(RST));
  not not_1 (not_1_out, register_1_q[1]);
  and and_1 (HALT, register_1_q[4], register_1_q[3], register_1_q[2], not_1_out, register_1_q[0]);

  // Notes on the sheet:
  //   contents of rom_1 (hex, n*v repeats v):
  //   804 11c0 19c2 400 28f0 30f0 0 4000 4801 0 58a4 60a0 68a2 0 78a4 80a0 88b0 91c0 99c2 0 a900 b110 0
  //   c008 c808 0 da00 e210 0 e800
endmodule
